// Logisim project CPU.circ as structural Verilog: 1 circuit, main circuit main
module main (
  input  [3:0] in_1,
  input  in_2
);

  wire and_1_out, and_2_out, and_3_out, and_4_out, clock_1_out, clock_2_out, decoder_1_out0, decoder_1_out1,
       decoder_1_out2, decoder_1_out3;
  wire [3:0] adder_1_out, PC_q;
  wire [7:0] adder_2_out, DataMemory_dout, InstructionMemory_dout, M0_q, M1_q, M2_q, M3_q, multiplexer_1_out,
       multiplexer_2_out, multiplexer_3_out, multiplexer_4_out, subtractor_1_out;

  Clock #(.highDuration(2), .lowDuration(2)) clock_1 (.out(clock_1_out));
  Register #(.width(4)) PC (.D(adder_1_out), .en(1'b1), .clk(clock_1_out), .Q(PC_q));  // open: clr
  Adder #(.width(4)) adder_1 (.a(in_1), .b(PC_q), .out(adder_1_out));  // open: cin, cout
  RAM #(.addrWidth(4)) InstructionMemory (
    .addr(PC_q), .oe(in_2), .clk(clock_1_out), .dout(InstructionMemory_dout));  // open: we, din
  Decoder #(.select(2)) decoder_1 (
    .out0(decoder_1_out0), .out1(decoder_1_out1), .out2(decoder_1_out2), .out3(decoder_1_out3),
    .sel(InstructionMemory_dout[5:4]));  // open: en
  Register M0 (.D(multiplexer_1_out), .en(and_1_out), .clk(clock_1_out), .Q(M0_q));  // open: clr
  and and_1 (and_1_out, decoder_1_out0, 1'b1);
  Register M1 (.D(multiplexer_1_out), .en(and_2_out), .clk(clock_1_out), .Q(M1_q));  // open: clr
  and and_2 (and_2_out, decoder_1_out1, 1'b1);
  Register M2 (.D(multiplexer_1_out), .en(and_3_out), .clk(clock_1_out), .Q(M2_q));  // open: clr
  and and_3 (and_3_out, decoder_1_out2, 1'b1);
  Register M3 (.D(multiplexer_1_out), .en(and_4_out), .clk(clock_1_out), .Q(M3_q));  // open: clr
  and and_4 (and_4_out, decoder_1_out3, 1'b1);
  Multiplexer #(.width(8)) multiplexer_1 (
    .in0(multiplexer_4_out), .in1(DataMemory_dout), .out(multiplexer_1_out), .sel(InstructionMemory_dout[7]));
  Multiplexer #(.select(2), .width(8)) multiplexer_2 (
    .in0(M0_q), .in1(M1_q), .in2(M2_q), .in3(M3_q), .out(multiplexer_2_out), .sel(InstructionMemory_dout[3:2]));
  Multiplexer #(.select(2), .width(8)) multiplexer_3 (
    .in0(M0_q), .in1(M1_q), .in2(M2_q), .in3(M3_q), .out(multiplexer_3_out), .sel(InstructionMemory_dout[1:0]));
  Adder adder_2 (.a(multiplexer_2_out), .b(multiplexer_3_out), .out(adder_2_out));  // open: cin, cout
  Subtractor subtractor_1 (.a(multiplexer_2_out), .b(multiplexer_3_out), .out(subtractor_1_out));  // open: bin, bout
  Multiplexer #(.width(8)) multiplexer_4 (
    .in0(adder_2_out), .in1(subtractor_1_out), .out(multiplexer_4_out), .sel(InstructionMemory_dout[6]));
  Clock clock_2 (.out(clock_2_out));
  RAM #(.addrWidth(2)) DataMemory (
    .addr(InstructionMemory_dout[3:2]), .oe(1'b1), .clk(clock_2_out), .din(multiplexer_4_out),
    .dout(DataMemory_dout));  // open: we

  // Notes on the sheet:
  //   in_1: initial=0x1
  //   in_2: initial=0x1
  //   CPU Project
  //   IF Stage
  //   Matthew McCaughan
  //   CPU Name: MARMalade
  //   Data for data memory must be hardcoded
  //   Input generated image file from assembler into Instruction Memory
  //   0-1: Reg 1
  //   2-3: Reg 2
  //   4-5: Dest. Reg.
  //   6-7: Control
  //   ID STAGE
  //   OPCODE
  //   00
  //   ADD: 00
  //   SUB: 01
  //   LDR: 10
  //   Left bit: controls if loading
  //   Right bit: Controls Adding/Subbing
  //   <----- WB STAGE
  //   Machine Code
  //   DEST REG
  //   00
  //   EX STAGE
  //   ALU
  //   REG 1
  //   REG 2
  //   00
  //   00
  //   ME STAGE
endmodule
